# Fritzing sketch distance (saved by Fritzing 0.9.5d)
breadboards: 1

parts:
  Composant1 = Arduino Uno (Rev3)
  hc-sr1 = hc-sr04

nets:
  N1: Composant1.D6_PWM, hc-sr1.Echo
  N2: Composant1.D7, hc-sr1.Trig
  5V: Composant1.5V, hc-sr1.VCC
  GND: Composant1.GND, hc-sr1.GND
