# Fritzing sketch ir (saved by Fritzing 0.9.5d)
breadboards: 1

parts:
  Composant1 = Arduino Uno (Rev3)
  IR1 = TSOP312.., 314.. [package=THT]

nets:
  N1: Composant1.D2, IR1.GND
  N2: Composant1.5V, IR1.Data
  N3: Composant1.GND, IR1.Vs
