# Fritzing sketch led-rgb (saved by Fritzing 0.9.5d)
breadboards: 1

parts:
  LED1 = RGB LED (com. cathode, rgb) [package="5 mm [THT]"]
  R1 = Resistor [tolerance=±5% resistance=220 package=THT]
  R2 = Resistor [tolerance=±5% resistance=220 package=THT]
  R3 = Resistor [tolerance=±5% resistance=220 package=THT]
  Composant1 = Arduino Uno (Rev3)

nets:
  N1: LED1.red_anode, R1.Pin_1
  N2: LED1.common_cathode, Composant1.GND
  N3: LED1.green_anode, R2.Pin_1
  N4: LED1.blue_anode, R3.Pin_1
  N5: R1.Pin_0, Composant1.D11_PWM/MOSI
  N6: R2.Pin_0, Composant1.D10_PWM/SS
  N7: R3.Pin_0, Composant1.D9_PWM
