# Fritzing sketch sensor_gas (saved by Fritzing 0.9.2b)
circuit board: 8.46667cm x 5.64444cm
breadboards: 1

parts:
  U1 = Spark Core (v1.0)
  J1 = Piezo Speaker
  U2 = GAS_SENSOR [package=mq-3]
  R1 = Resistor [tolerance=±5% resistance=10k package=THT]
  R2 = Resistor [tolerance=±5% resistance=10k package=THT]

nets:
  N1: U1.A0, U2.B1, R1.Pin_1
  N2: U1.A2, U1.3V3
  N3: U1.A3, U1.A6
  N4: U1.A5, U1.VIN, U2.A1, U2.H1
  N5: U1.GND, J1.pin1, U2.H2, R2.Pin_0
  N6: U1.D1, J1.pin2
  N7: R1.Pin_0, R2.Pin_1

custom parts:
  Spark Core (v1.0): The Spark Core is a tiny Wi-Fi development board that makes it easy to create internet-connected hardware. The Core is all you need to get started; power it over USB and in minutes you'll be controlling LEDs, switches and motors and collecting data from sensors over the internet! It has 8 digital I/O pins, 8 analog I/O pins, 8 PWM pins; UART (Serial), SPI, I2C, and JTAG peripherals available.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

// code stored in the sketch: sensor_gas.ino
int buzzerPin = D1;
int sensorPin = A0;
int energia = A5;
int valorSensor = 0;
int limite = 4000;

void setup() {
    pinMode(buzzerPin, OUTPUT);
    //pinMode(sensorPin, INPUT);
    Serial.begin(9600);
}

void loop() {
    //digitalWrite(energia, HIGH);
    valorSensor = analogRead(sensorPin);
    Serial.println(valorSensor);
    //Particle.variable("valorSensor", valorSensor);
    if (valorSensor > limite)
    { //buzzer vai "piscar"
        Serial.println(limite, valorSensor);
        /*delay(200);
        digitalWrite(buzzerPin, HIGH);
        delay(200);
        digitalWrite(buzzerPin, LOW);*/
    }
}
